// Logisim project mar.circ as structural Verilog
module main (
);

  wire clock_1_out, demultiplexer_1_out1, demultiplexer_1_out4;
  wire [1:0] controlunit_1_mw;
  wire [2:0] controlunit_1_p0, controlunit_1_p3;
  wire [3:0] multiplexer_1_out, multiplexer_1_out_2, multiplexer_1_out_3, multiplexer_1_out_4;
  wire [11:0] MAR_q;
  wire [15:0] AC_q, ram_1_dout, undriven, undriven_2, undriven_3, undriven_4, undriven_5;

  Clock clock_1 (.out(clock_1_out));
  Demultiplexer #(.select(3)) demultiplexer_1 (
    .out1(demultiplexer_1_out1), .out4(demultiplexer_1_out4), .in(1'b1), .sel(controlunit_1_p3));  // open: out0, out2, out3, out5, out6, out7
  RAM #(.addrWidth(12), .dataWidth(16)) ram_1 (
    .addr(MAR_q), .we(controlunit_1_mw[0]), .oe(controlunit_1_mw[1]), .clk(clock_1_out),
    .din({multiplexer_1_out_4, multiplexer_1_out_3, multiplexer_1_out_2, multiplexer_1_out}),
    .dout(ram_1_dout));
  Register #(.width(12)) MAR (.D(12'h5), .en(demultiplexer_1_out1), .clk(clock_1_out), .Q(MAR_q));  // open: clr
  Register #(.width(16)) AC (.D({16{1'b0}}), .en(demultiplexer_1_out4), .clk(clock_1_out), .Q(AC_q));  // open: clr
  ControlUnit controlunit_1 (
    .P0(controlunit_1_p0[0]), .P1(controlunit_1_p0[1]), .P2(controlunit_1_p0[2]), .P3(controlunit_1_p3[0]),
    .P4(controlunit_1_p3[1]), .P5(controlunit_1_p3[2]), .Mr(controlunit_1_mw[1]), .Mw(controlunit_1_mw[0]));  // open: IRopcode, RingCounter, A0, A1, Cr, Lalt
  Multiplexer #(.select(3), .width(16)) multiplexer_1 (
    .in0(ram_1_dout), .in1({4'b0000, MAR_q}), .in2(undriven_2), .in3(undriven), .in4(AC_q), .in5(undriven_3),
    .in6(undriven_4), .in7(undriven_5),
    .out({multiplexer_1_out_4, multiplexer_1_out_3, multiplexer_1_out_2, multiplexer_1_out}),
    .sel(controlunit_1_p0));
  Hex_Digit_Display hex_digit_display_1 (.value(multiplexer_1_out_4));  // open: dp
  Hex_Digit_Display hex_digit_display_2 (.value(multiplexer_1_out_3));  // open: dp
  Hex_Digit_Display hex_digit_display_3 (.value(multiplexer_1_out_2));  // open: dp
  Hex_Digit_Display hex_digit_display_4 (.value(multiplexer_1_out));  // open: dp

  // Notes on the sheet:
  //   p5 p4 p3
  //   p2 p1 p0
  //   Data Bus
endmodule

module cyclecount (
  input  Clock,
  input  Cr,
  output T0,
  output T1,
  output T2,
  output T3,
  output T4
);

  or or_1 (T0, T4, T3, T2, T1);
  D_Flip_Flop D0 (.D(T0), .clk(Clock), .Q(T1), .reset(Cr));  // open: Qn, preset
  D_Flip_Flop D1 (.D(T1), .clk(Clock), .Q(T2), .reset(Cr));  // open: Qn, preset
  D_Flip_Flop D2 (.D(T2), .clk(Clock), .Q(T3), .reset(Cr));  // open: Qn, preset
  D_Flip_Flop D3 (.D(T3), .clk(Clock), .Q(T4), .reset(Cr));  // open: Qn, preset

  // Notes on the sheet:
  //   clock
  //   Cr
endmodule

module testkeyboard (
  input  b0,
  input  b1,
  input  b2,
  input  b3,
  input  b4,
  input  b5,
  input  b6,
  input  b7,
  input  b8,
  input  b9,
  input  bA,
  input  bB,
  input  bC,
  input  bD,
  input  bE,
  input  bF,
  output [3:0] keyout
);

  Priority_Encoder #(.select(4)) priority_encoder_1 (
    .in0(b0), .in1(b1), .in2(b2), .in3(b3), .in4(b4), .in5(b5), .in6(b6), .in7(b7), .in8(b8), .in9(b9),
    .in10(bA), .in11(bB), .in12(bC), .in13(bD), .in14(bE), .in15(bF), .out(keyout));  // open: gs, en_out, en_in
endmodule

module ControlUnit (
  input  [3:0] IRopcode,
  input  [7:0] RingCounter,
  output P0,
  output P1,
  output P2,
  output P3,
  output P4,
  output P5,
  output A0,
  output A1,
  output Cr,
  output Mr,
  output Mw,
  output Lalt
);

  wire and_1_out, and_2_out, and_3_out, decoder_1_out0, decoder_1_out1, decoder_1_out2, decoder_1_out3;

  Decoder #(.select(4)) decoder_1 (
    .out0(decoder_1_out0), .out1(decoder_1_out1), .out2(decoder_1_out2), .out3(decoder_1_out3),
    .out4(RingCounter[5]), .sel(IRopcode), .en(1'b1));  // open: out5, out6, out7, out8, out9, out10, out11, out12, out13, out14, out15
  buf out0 (P0, and_1_out);  // OR_Gate
  and and_1 (and_1_out, RingCounter[3], RingCounter[5]);
  buf out1 (P1, and_1_out);  // OR_Gate
  and and_2 (and_2_out, RingCounter[4], RingCounter[5]);
  and and_3 (and_3_out, RingCounter[5], RingCounter[5]);
  buf out2 (P2, and_1_out);  // OR_Gate
  or out3 (P3, and_1_out, and_2_out);
  buf out4 (P4, and_2_out);  // OR_Gate
  buf out5 (P5, and_3_out);  // OR_Gate
  buf outA0 (A0, and_3_out);  // OR_Gate
  // OR_Gate outA1 has open pins: out=A1
  buf outCr (Cr, and_3_out);  // OR_Gate
  buf outMr (Mr, and_2_out);  // OR_Gate
  // OR_Gate outMw has open pins: out=Mw
  buf outLalt (Lalt, and_3_out);  // OR_Gate

  // Notes on the sheet:
  //   ADD=0011
endmodule
